// Logisim project task2.circ as structural Verilog: 1 circuit, main circuit main
module main (
  input  A,
  input  B,
  output LED1,
  output LED2
);

  wire nor_1_out, nor_2_out, nor_3_out, nor_4_out, nor_5_out, nor_6_out, nor_7_out, nor_8_out;

  nor nor_1 (nor_1_out, B, B);
  // OR_Gate or_1 has open pins: in0=B, in1=B, out=open
  // OR_Gate or_2 has open pins: in0=A, in1=A, out=open
  nor nor_2 (nor_2_out, A, A);
  // OR_Gate or_3 has open pins: in0=A, in1=B, out=open
  nor nor_3 (nor_3_out, A, B);
  // OR_Gate or_4 has open pins: in0=A, in1=nor_1_out, out=open
  nor nor_4 (nor_4_out, A, nor_1_out);
  nor nor_5 (nor_5_out, nor_1_out, nor_2_out);
  // OR_Gate or_5 has open pins: in0=nor_1_out, in1=nor_2_out, out=open
  nor nor_6 (nor_6_out, A, nor_3_out);
  // OR_Gate or_6 has open pins: in0=A, in1=nor_3_out, out=open
  // OR_Gate or_7 has open pins: in0=nor_3_out, in1=B, out=open
  nor nor_7 (nor_7_out, nor_3_out, B);
  // OR_Gate or_8 has open pins: in0=nor_4_out, in1=nor_5_out, out=open
  nor nor_8 (nor_8_out, nor_4_out, nor_5_out);
  nor nor_9 (LED1, nor_6_out, nor_7_out);
  // OR_Gate or_9 has open pins: in0=nor_6_out, in1=nor_7_out, out=open
  nor nor_10 (LED2, nor_8_out, nor_8_out);
  // OR_Gate or_10 has open pins: in0=nor_8_out, in1=nor_8_out, out=open
endmodule
