// Logisim project task3_1Blue.circ as structural Verilog: 1 circuit, main circuit main
module main (
  input  M,
  input  P,
  input  C,
  output Blue
);

  wire and_1_out, and_2_out;

  and and_1 (and_1_out, M, P);
  and and_2 (and_2_out, M, C);
  or or_1 (Blue, and_1_out, and_2_out);
endmodule
