// Logisim project task3_2red.circ as structural Verilog: 1 circuit, main circuit main
module main (
  input  H,
  input  C,
  input  P,
  input  M,
  output Red
);

  wire or_1_out, or_2_out;

  or or_1 (or_1_out, H, C);
  or or_2 (or_2_out, or_1_out, P);
  and and_1 (Red, or_2_out, M);
endmodule
