// Logisim project task3_3Green.circ as structural Verilog: 1 circuit, main circuit main
module main (
  input  H,
  input  P,
  input  M,
  input  F,
  output Green
);

  wire or_1_out, or_2_out;

  or or_1 (or_1_out, H, P);
  or or_2 (or_2_out, M, F);
  and and_1 (Green, or_1_out, or_2_out);
endmodule
