// Logisim project task3_4Blue.circ as structural Verilog: 1 circuit, main circuit main
module main (
  input  C,
  input  P,
  input  M,
  input  F,
  output Blue2
);

  wire and_1_out, or_1_out;

  and and_1 (and_1_out, C, P);
  or or_1 (or_1_out, M, F);
  and and_2 (Blue2, and_1_out, or_1_out);
endmodule
