// Logisim project car_secure.circ as structural Verilog: 1 circuit, main circuit main
module main (
  input  K,
  input  C,
  input  S,
  output E,
  output B
);

  wire and_1_out, nand_1_out;

  and and_1 (and_1_out, C, S);
  nand nand_1 (nand_1_out, C, S);
  and and_2 (E, K, and_1_out);
  and and_3 (B, K, nand_1_out);
endmodule
