// Logisim project unsign_integer.circ as structural Verilog: 1 circuit, main circuit main
module main (
  input  A,
  input  B,
  input  C,
  input  D,
  output odd
);

  wire nand_1_out, or_1_out;

  or or_1 (or_1_out, B, C);
  nand nand_1 (nand_1_out, or_1_out, D);
  and and_1 (odd, A, nand_1_out);
endmodule
