// Logisim project 3_1task.circ as structural Verilog: 1 circuit, main circuit main
module main (
  input  A,
  input  B,
  input  C,
  output LED1,
  output LED2,
  output LED3,
  output LED4,
  output LED5
);

  wire and_1_out, or_3_out;

  or or_1 (LED1, A, B, C);
  or or_2 (LED2, A, B);
  and and_1 (and_1_out, B, C);
  or or_3 (or_3_out, B, C);
  or or_4 (LED3, A, and_1_out);
  and and_2 (LED5, or_3_out, A);

  assign LED4 = A;
endmodule
