// Logisim project 3_4task_CPE.circ as structural Verilog: 2 circuits, main circuit main
module main (
  input  A,
  input  B,
  input  C,
  input  A_2,
  input  B_2,
  input  C_2,
  input  A_3,
  input  B_3,
  input  C_3
);

  wire sub_1_a_2, sub_1_b_2, sub_1_c_2, sub_1_d, sub_1_e, sub_1_f, sub_1_g, sub_2_a_2, sub_2_b_2, sub_2_c_2,
       sub_2_d, sub_2_e, sub_2_f, sub_2_g, sub_3_a_2, sub_3_b_2, sub_3_c_2, sub_3_d, sub_3_e, sub_3_f,
       sub_3_g;

  sub sub_1 (
    .a(A), .b(B), .c(C), .a_2(sub_1_a_2), .b_2(sub_1_b_2), .c_2(sub_1_c_2), .d(sub_1_d), .e(sub_1_e),
    .f(sub_1_f), .g(sub_1_g));
  sub sub_2 (
    .a(A_2), .b(B_2), .c(C_2), .a_2(sub_2_a_2), .b_2(sub_2_b_2), .c_2(sub_2_c_2), .d(sub_2_d), .e(sub_2_e),
    .f(sub_2_f), .g(sub_2_g));
  sub sub_3 (
    .a(A_3), .b(B_3), .c(C_3), .a_2(sub_3_a_2), .b_2(sub_3_b_2), .c_2(sub_3_c_2), .d(sub_3_d), .e(sub_3_e),
    .f(sub_3_f), .g(sub_3_g));
  _7_Segment_Display u_7_segment_display_1 (
    .g(sub_1_g), .f(sub_1_f), .a(sub_1_a_2), .b(sub_1_b_2), .e(sub_1_e), .d(sub_1_d), .c(sub_1_c_2));  // open: dp
  _7_Segment_Display u_7_segment_display_2 (
    .g(sub_2_g), .f(sub_2_f), .a(sub_2_a_2), .b(sub_2_b_2), .e(sub_2_e), .d(sub_2_d), .c(sub_2_c_2));  // open: dp
  _7_Segment_Display u_7_segment_display_3 (
    .g(sub_3_g), .f(sub_3_f), .a(sub_3_a_2), .b(sub_3_b_2), .e(sub_3_e), .d(sub_3_d), .c(sub_3_c_2));  // open: dp
endmodule

module sub (
  input  a,
  input  b,
  input  c,
  output a_2,
  output b_2,
  output c_2,
  output d,
  output e,
  output f,
  output g
);

  not not_1 (d, b);
  not not_2 (g, a);

  assign a_2 = 1'b1;
  assign b_2 = b;
  assign c_2 = 1'b0;
  assign e = 1'b1;
  assign f = 1'b1;
endmodule
