// Logisim project task1_mux.circ as structural Verilog: 1 circuit, main circuit main
module main (
  input  A,
  input  in_2,
  input  B,
  input  in_4,
  input  in_5,
  input  in_6,
  output LED_RED,
  output LED_GREEN
);

  wire and_1_out, and_2_out, and_3_out, and_4_out, not_1_out, not_2_out;

  not not_1 (not_1_out, A);
  not not_2 (not_2_out, B);
  and and_1 (and_1_out, in_2, not_2_out, not_1_out);
  and and_2 (and_2_out, in_4, not_1_out, B);
  and and_3 (and_3_out, in_5, A, not_2_out);
  and and_4 (and_4_out, in_6, B, A);
  or or_1 (LED_GREEN, and_1_out, and_2_out, and_3_out, and_4_out);
  not not_3 (LED_RED, LED_GREEN);
endmodule
