// Logisim project task2_2.circ as structural Verilog: 2 circuits, main circuit main
module main (
  input  A,
  input  B,
  input  C,
  input  D
);

  wire not_1_out, odd_check_1_out_5, odd_check_2_out_5, xor_1_out;

  not not_1 (not_1_out, A);
  odd_check odd_check_1 (.A(A), .B(B), .C(C), .D(D), .out_5(odd_check_1_out_5));
  odd_check odd_check_2 (.A(not_1_out), .B(B), .C(C), .D(D), .out_5(odd_check_2_out_5));
  xor xor_1 (xor_1_out, odd_check_2_out_5, odd_check_1_out_5);
  LED Error_Indicator (.in(xor_1_out));
endmodule

module odd_check (
  input  A,
  input  B,
  input  C,
  input  D,
  output out_5
);

  wire xnor_1_out, xnor_2_out;

  xnor xnor_1 (xnor_1_out, A, B);
  xnor xnor_2 (xnor_2_out, xnor_1_out, C);
  xnor xnor_3 (out_5, xnor_2_out, D);
endmodule
