// Logisim project task_3.circ as structural Verilog: 2 circuits, main circuit main
module main (
  input  in_1,
  input  in_2,
  input  in_3,
  input  in_4,
  input  in_5,
  input  in_6,
  input  in_7,
  input  in_8,
  output LED___FAIL,
  output LED___SUCCESS
);

  sub sub_1 (
    .in_1(in_1), .in_2(in_2), .in_3(in_3), .in_4(in_4), .in_5(in_5), .in_6(in_6), .in_7(in_7), .in_8(in_8),
    .out_9(LED___SUCCESS));
  not not_1 (LED___FAIL, LED___SUCCESS);
endmodule

module sub (
  input  in_1,
  input  in_2,
  input  in_3,
  input  in_4,
  input  in_5,
  input  in_6,
  input  in_7,
  input  in_8,
  output out_9
);

  wire xnor_1_out, xnor_2_out, xnor_3_out, xnor_4_out;

  xnor xnor_1 (xnor_1_out, in_1, in_5);
  xnor xnor_2 (xnor_2_out, in_2, in_6);
  xnor xnor_3 (xnor_3_out, in_3, in_7);
  xnor xnor_4 (xnor_4_out, in_4, in_8);
  and and_1 (out_9, xnor_1_out, xnor_2_out, xnor_3_out, xnor_4_out);
endmodule
