// Logisim project task1.circ as structural Verilog: 1 circuit, main circuit main
module main (
  input  Input,
  output D
);

  wire Clock_out;

  Clock Clock (.out(Clock_out));
  D_Flip_Flop d_ff_1 (.clk(Clock_out), .D(Input), .Q(D));  // open: Qn, preset, en, reset
endmodule
