// Logisim project task2.circ as structural Verilog: 1 circuit, main circuit main
module main (
  input  I,
  output Output,
  output DA,
  output DB
);

  wire and_1_out, and_2_out, clock_1_out, nor_1_out, or_1_out;

  Clock clock_1 (.out(clock_1_out));
  D_Flip_Flop d_ff_1 (.clk(clock_1_out), .D(and_1_out), .Q(DA));  // open: Qn, preset, en, reset
  D_Flip_Flop d_ff_2 (.clk(clock_1_out), .D(and_2_out), .Q(DB));  // open: Qn, preset, en, reset
  or or_1 (or_1_out, DA, DB);
  nor nor_1 (nor_1_out, DA, DB);
  and and_1 (and_1_out, or_1_out, I);
  and and_2 (and_2_out, I, nor_1_out);

  assign Output = DB;
endmodule
