// Logisim project task1.circ as structural Verilog: 1 circuit, main circuit main
module main (
  input  L,
  input  R,
  input  H
);

  wire and_1_out, and_2_out, and_3_out, and_4_out, and_5_out, and_6_out, and_7_out, and_8_out, and_9_out,
       and_10_out, and_11_out, and_12_out, clock_1_out, d_ff_1_q, d_ff_2_q, d_ff_3_q, nand_1_out, nand_2_out,
       or_1_out, or_2_out, or_3_out, or_4_out, or_5_out, or_6_out;

  Clock clock_1 (.out(clock_1_out));
  or or_1 (or_1_out, L, R);
  or or_2 (or_2_out, L, H);
  or or_3 (or_3_out, H, R);
  and and_1 (and_1_out, or_1_out, nand_2_out);
  and and_2 (and_2_out, d_ff_1_q, nand_2_out);
  and and_3 (and_3_out, d_ff_2_q, nand_2_out);
  or or_4 (or_4_out, and_1_out, H);
  or or_5 (or_5_out, and_2_out, H);
  or or_6 (or_6_out, and_3_out, H);
  and and_4 (and_4_out, or_4_out, nand_1_out);
  and and_5 (and_5_out, or_5_out, nand_1_out);
  and and_6 (and_6_out, or_6_out, nand_1_out);
  D_Flip_Flop d_ff_1 (.clk(clock_1_out), .D(and_4_out), .Q(d_ff_1_q));  // open: Qn, preset, en, reset
  D_Flip_Flop d_ff_2 (.clk(clock_1_out), .D(and_5_out), .Q(d_ff_2_q));  // open: Qn, preset, en, reset
  D_Flip_Flop d_ff_3 (.clk(clock_1_out), .D(and_6_out), .Q(d_ff_3_q));  // open: Qn, preset, en, reset
  nand nand_1 (nand_1_out, d_ff_3_q, d_ff_2_q, d_ff_1_q);
  nand nand_2 (nand_2_out, d_ff_1_q, d_ff_2_q, d_ff_3_q);
  and and_7 (and_7_out, or_2_out, d_ff_1_q);
  and and_8 (and_8_out, or_2_out, d_ff_2_q);
  and and_9 (and_9_out, or_2_out, d_ff_3_q);
  LED L3 (.in(and_9_out));
  LED L2 (.in(and_8_out));
  LED L1 (.in(and_7_out));
  LED R3 (.in(and_10_out));
  LED R2 (.in(and_12_out));
  and and_10 (and_10_out, or_3_out, d_ff_1_q);
  and and_11 (and_11_out, or_3_out, d_ff_2_q);
  and and_12 (and_12_out, or_3_out, d_ff_3_q);
  LED R1 (.in(and_11_out));
endmodule
